# Fritzing sketch screen (saved by Fritzing 0.9.9b)
breadboards: 1

parts:
  U1 = NodeMCU V1.0
  Part1 = LCD1602-I2C
  DispMod+ = KY-004 Key Switch Module [package="Breakout board"]
  Mod3 = KY-004 Key Switch Module [package="Breakout board"]
  Mod4 = KY-004 Key Switch Module [package="Breakout board"]
  Mod5 = KY-004 Key Switch Module [package="Breakout board"]
  Mod6 = KY-012 Active Buzzer Module [package="Breakout board"]

nets:
  N1: U1.D1, Part1.SCL
  N2: U1.D2, Part1.SDA
  N3: U1.D3, DispMod+.S
  N4: U1.D4, Mod3.S
  GND: U1.GND, Part1.GND, DispMod+.-, Mod3.-, Mod4.-, Mod5.-, Mod6.-
  N5: U1.D5, Mod4.S
  N6: U1.D6, Mod5.S
  N7: U1.D8, Mod6.S
  VIN: U1.Vin, Part1.VCC

custom parts:
  NodeMCU V1.0: ESP8266 based NodeMCU
  LCD1602-I2C: A standard character display, usually with 2x16 characters. Comes in many colors with LCM1602 IIC attached.
  KY-004 Key Switch Module: Arduino Key Switch Module Keyes KY-004 is a push button that will output a high signal when pressed.
  KY-012 Active Buzzer Module: Active Piezoelectric Buzzer Module KY-012, it produces single-tone sound when signal is high. (Special thanks to vanepp for fixing the PCB holes and other errors)
