# Fritzing sketch sensors (saved by Fritzing 0.9.9b)
breadboards: 1

parts:
  U1 = NodeMCU V1.0
  Mod1 = KY-015 Temperature & Humidity Sensor Module [package="Breakout board"]
  Mod2 = KY-016 RGB Full Color LED Module [package="Breakout board"]
  Mod3 = KY-018 Photoresistor Module [package="Breakout board"]
  Mod4 = KY-026 Flame Sensor Module [package="Breakout board"]
  R1 = Resistor [tolerance=±5% power=0.25 resistance=220 package=THT]
  LED1 = LED - 5mm [color="White (6500K)" current=0.030 package="5 mm [THT]"]

nets:
  N1: U1.D1, Mod4.D0
  N2: U1.D2, Mod1.Vin
  N3: U1.3V3, Mod4.+
  N4: U1.GND, Mod1.-, Mod2.-, Mod3.S, Mod4.G, R1.Pin_1
  N5: U1.D5, LED1.anode
  N6: U1.D6, Mod2.R
  N7: U1.D7, Mod2.G
  N8: U1.D8, Mod2.B
  N9: U1.Vin, Mod1.S, Mod3.-
  N10: U1.A0, Mod3.Vin
  N11: R1.Pin_0, LED1.cathode

custom parts:
  NodeMCU V1.0: ESP8266 based NodeMCU
  KY-015 Temperature & Humidity Sensor Module: KY-015 temperature and humidity sensor module, provides a low-latency serial interface to measure humidity and temperature.
  KY-016 RGB Full Color LED Module: KY-016 Arduino full color 5mm RGB LED, different colors can be obtained by mixing the three primary colors.
  KY-018 Photoresistor Module: KY-018 Photoresistor module, used to measure light intensity. It can determine the presence or absence of light.
  KY-026 Flame Sensor Module: KY-026 Flame Sensor Module reacts in the presence of fire.
